# Fritzing sketch 2017-Firefighter (saved by Fritzing 0.9.3b)
breadboards: 1

parts:
  Controller = Arduino Mega 2560 (Rev3)
  Other = L298 [package=multiwatt15_6400bgheatsink]
  Power_Switch = LIPO-2000mAh [package=lipo-2000]
  MC1 = L298 [package=multiwatt15_6400bgheatsink]
  Right_1 = DC Motor
  Strafe = DC Motor
  Right_2 = DC Motor
  S1 = SPST Switch [package=switch-spdt-smd]
  Flame_Sensor = TSOP312.., 314.. [package=THT]
  Start_Mic = Breakout Board for Electret Microphone
  Back_Ultrasonic = hc-sr04
  Front_Ultrasonic = hc-sr04
  Right_Ultrasonic = hc-sr04
  Left_Ultrasonic = hc-sr04
  Nav = Triple Axis Gyro Breakout ITG-3200
  MC2 = L298 [package=multiwatt15_6400bgheatsink]
  Left_2 = DC Motor
  Left_1 = DC Motor
  5V = Voltage Regulator [package=to220-igo]
  Extinguisher = DC Motor
  Raspberry_Pi_1 = Raspberry Pi 3 [part_number=RPI-3-V1.2]
  LED1 = LED - 5mm [color="Red (633nm)" package="5 mm [THT]"]
  LED2 = LED - 5mm [color="Yellow (595nm)" package="5 mm [THT]"]
  R1 = Resistor [tolerance=±5% resistance=220 package="2010 [SMD]"]
  S2 = SWITCH-MOMENTARY-2 [package=reed_switch_pth]
  R2 = Resistor [tolerance=±5% resistance=220 package="2010 [SMD]"]

nets:
  N1: Controller.A0, Start_Mic.AUD
  N2: Controller.D21/SCL, Controller.SCL, Nav.SCL
  N3: Controller.D20/SDA, Nav.SDA
  GND: Controller.GND, Flame_Sensor.GND, Start_Mic.GND, Left_Ultrasonic.GND, Nav.GND, 5V.GND
  N4: Controller.D13_PWM, MC1.IN4
  N5: Controller.D12_PWM, MC1.IN3
  N6: Controller.D11_PWM, MC1.IN2
  N7: Controller.D10_PWM, MC1.IN1
  N8: Controller.D9_PWM, MC2.IN4
  N9: Controller.D8_PWM, MC2.IN3
  VCC: Controller.5V, Flame_Sensor.Vs, Start_Mic.VCC, Nav.VCC, 5V.IN
  N10: Controller.D2_PWM, Nav.INT
  N11: Controller.D4_PWM, Other.IN3
  N12: Controller.D5_PWM, Other.IN4
  N13: Controller.D6_PWM, MC2.IN1
  N14: Controller.D7_PWM, MC2.IN2
  N15: Controller.D22, Front_Ultrasonic.Echo
  N16: Controller.D23, Front_Ultrasonic.Trig
  N17: Controller.D24, Left_Ultrasonic.Echo
  N18: Controller.D25, Left_Ultrasonic.Trig
  N19: Controller.D26, Right_Ultrasonic.Echo
  N20: Controller.D27, Right_Ultrasonic.Trig
  N21: Controller.D28, Back_Ultrasonic.Echo
  N22: Controller.D29, Back_Ultrasonic.Trig
  N23: Controller.D37, Flame_Sensor.Data
  N24: Controller.D44, Other.IN2
  N25: Controller.D45, Other.IN1
  N26: Other.OUT1, Extinguisher.pin_2
  N27: Other.OUT2, Extinguisher.pin_1
  GND_2: Other.GND, Power_Switch.-, MC1.GND, MC2.GND
  N28: Other.OUT3, Strafe.pin_2
  N29: Other.OUT4, Strafe.pin_1
  N30: Other.CSB, MC1.CSB, S1.P, MC2.CSB
  N31: Power_Switch.+, S1.S
  N32: MC1.OUT1, Right_2.pin_2
  N33: MC1.OUT2, Right_2.pin_1
  N34: MC1.OUT3, Right_1.pin_2
  N35: MC1.OUT4, Right_1.pin_1
  VCC_2: Back_Ultrasonic.VCC, Front_Ultrasonic.VCC, Right_Ultrasonic.VCC, Left_Ultrasonic.VCC, 5V.OUT
  GND_3: Back_Ultrasonic.GND, Front_Ultrasonic.GND, Right_Ultrasonic.GND
  N36: MC2.OUT1, Left_2.pin_2
  N37: MC2.OUT2, Left_2.pin_1
  N38: MC2.OUT3, Left_1.pin_2
  N39: MC2.OUT4, Left_1.pin_1
  N40: Raspberry_Pi_1.3V3, S2.1
  N41: Raspberry_Pi_1.GPIO19, LED2.anode
  N42: Raspberry_Pi_1.GPIO26, LED1.anode
  N43: Raspberry_Pi_1.GND, R1.Pin_1, R2.Pin_0
  N44: Raspberry_Pi_1.GPIO23, S2.2, R2.Pin_1
  N45: LED1.cathode, LED2.cathode, R1.Pin_0

custom parts:
  hc-sr04: This is a HC-SR04 Distance Sensor

// code stored in the sketch: firefighter.ino


void setup() {
  // put your setup code here, to run once:
  pinMode(A0, OUTPUT);
	pinMode(A1, OUTPUT);
}

void loop() {
  // put your main code here, to run repeatedly:
  digitalWrite(A0, HIGH);
}

// code stored in the sketch: TwoWheelRobot.ino


void setup() {
  // put your setup code here, to run once:
  pinMode(A0, OUTPUT);
	pinMode(A1, OUTPUT);
}

void loop() {
  // put your main code here, to run repeatedly:
  digitalWrite(A0, HIGH);
}
